# Fritzing sketch Sketch (saved by Fritzing 0.9.3b)
circuit board: 8.46667cm x 5.64444cm
breadboards: 1

parts:
  U1 = NodeMCU V1.0
  RHT1 = Humidity and Temperature Sensor RHT03

nets:
  N1: U1.D2, RHT1.Vcc
  N2: U1.3V3, RHT1.GND_2
  N3: U1.GND, RHT1.GND_1

custom parts:
  NodeMCU V1.0: ESP8266 based NodeMCU
