# Fritzing sketch Sketch (saved by Fritzing 0.9.3b)
breadboards: 1

parts:
  U1 = NodeMCU V1.0
  R1 = Rotary Potentiometer (Small) [maximum_resistance=100kΩ package=THT]
  LED1 = LED - 5mm [color="Red (633nm)" package="5 mm [THT]"]
  R2 = Resistor [tolerance=±5% resistance=220 package=THT]

nets:
  N1: U1.D1, R1.wiper
  N2: U1.D2, LED1.anode
  N3: U1.GND, R1.leg2, R2.Pin_1
  N4: LED1.cathode, R2.Pin_0

custom parts:
  NodeMCU V1.0: ESP8266 based NodeMCU
