# Fritzing sketch 烧录板Sketch (saved by Fritzing 0.9.3b)
perfboards: 1

parts:
  J1 = female pin header, 2 pins [form="♀ (female)"]
  J2 = female pin header, 2 pins [form="♀ (female)"]  # not connected
  S1 = Toggle Switch [package=THT]
  S2 = Pushbutton [package="[THT]"]

nets:
  N1: J1.pin1, S1.COM
  N2: S2.Pin_1, S2.Pin_2
  N3: S2.Pin_3, S2.Pin_4
